# Fritzing sketch dual-distancesensor (saved by Fritzing 0.9.3b)
breadboards: 1

parts:
  Raspberry_Pi_1 = Raspberry Pi 3 [part_number=RPI-3-V1.2]
  hc-sr1 = hc-sr04
  R1 = Resistor [tolerance=±5% resistance=330 package=THT]
  R2 = Resistor [tolerance=±5% resistance=330 package=THT]
  R3 = Resistor [tolerance=±5% resistance=100 package=THT]
  hc-sr2 = hc-sr04
  R4 = Resistor [tolerance=±5% resistance=330 package=THT]
  R5 = Resistor [tolerance=±5% resistance=100 package=THT]
  R6 = Resistor [tolerance=±5% resistance=330 package=THT]

nets:
  N1: Raspberry_Pi_1.GIPO8, R4.Pin_1, R6.Pin_1
  N2: Raspberry_Pi_1.GIPO25, hc-sr2.Trig
  N3: Raspberry_Pi_1.GIPO24, R1.Pin_1, R2.Pin_1
  N4: Raspberry_Pi_1.GIPO23, hc-sr1.Trig
  GND: Raspberry_Pi_1.GND, hc-sr1.GND, R3.Pin_0, hc-sr2.GND, R5.Pin_0
  VCC: Raspberry_Pi_1.5V, hc-sr1.VCC, hc-sr2.VCC
  N5: hc-sr1.Echo, R1.Pin_0
  N6: R2.Pin_0, R3.Pin_1
  N7: hc-sr2.Echo, R4.Pin_0
  N8: R5.Pin_1, R6.Pin_0
